// Logisim project konwerter n2 - u2.circ as structural Verilog: 1 circuit, main circuit main
module main (
  input  a,
  input  b,
  input  c,
  input  d
);

  wire _1_2_out, _1_3_out, _1_4_out, _1_5_out, _1_out, _2_2_out, _2_3_out, _2_4_out, _2_5_out, _2_6_out,
       _2_7_out, _2_out, _3_2_out, _3_3_out, _3_4_out, _3_5_out, _3_out, not_1_out, not_2_out, not_3_out,
       not_4_out;

  not _1 (_1_out, b);
  not _1_2 (_1_2_out, c);
  not _1_3 (_1_3_out, d);
  nand _1_4 (_1_4_out, _1_out, _1_2_out, _1_3_out);
  nand _3 (_3_out, a, d);
  not _3_2 (_3_2_out, c);
  nand _3_3 (_3_3_out, _3_out, c);
  nand _3_4 (_3_4_out, a, _3_2_out, d);
  nand _2 (_2_out, _1_2_out, _1_3_out, a);
  nand _1_5 (_1_5_out, a, _1_4_out);
  nand _3_5 (_3_5_out, _3_3_out, _3_4_out);
  not not_1 (not_1_out, _1_5_out);
  and _2_2 (_2_2_out, _2_out, a);
  nand _2_3 (_2_3_out, a, _1_out);
  nand _2_4 (_2_4_out, _1_2_out, _1_3_out);
  not not_2 (not_2_out, _2_4_out);
  nand _2_5 (_2_5_out, _2_2_out, b);
  not not_3 (not_3_out, _2_5_out);
  nor _2_6 (_2_6_out, _2_3_out, not_2_out);
  nor _2_7 (_2_7_out, not_3_out, _2_6_out);
  LED x1 (.in(not_1_out));
  LED x2 (.in(not_4_out));
  not not_4 (not_4_out, _2_7_out);
  LED x3 (.in(_3_5_out));
  LED x4 (.in(d));
endmodule
