// Logisim project licznik asynch mod 9-13.circ as structural Verilog: 1 circuit, main circuit licznik asynchroniczny mod 9/13
module licznik_asynchroniczny_mod_9_13 (
  input  in_1
);

  wire and_1_out, and_2_out, button_1_out, j_k_ff_1_q, j_k_ff_1_qn, j_k_ff_2_q, j_k_ff_2_qn, j_k_ff_3_q,
       j_k_ff_3_qn, j_k_ff_4_qn, not_1_out, or_1_out;

  Button button_1 (.out(button_1_out));
  J_K_Flip_Flop j_k_ff_1 (
    .J(1'b1), .clk(button_1_out), .K(1'b1), .Q(j_k_ff_1_q), .Qn(j_k_ff_1_qn), .preset(or_1_out));  // open: en, reset
  LED led_1 (.in(j_k_ff_3_qn));
  LED led_2 (.in(j_k_ff_4_qn));
  J_K_Flip_Flop j_k_ff_2 (
    .J(1'b1), .clk(j_k_ff_1_q), .K(1'b1), .Q(j_k_ff_2_q), .Qn(j_k_ff_2_qn), .preset(or_1_out));  // open: en, reset
  not not_1 (not_1_out, in_1);
  LED led_3 (.in(j_k_ff_2_qn));
  LED led_4 (.in(j_k_ff_1_qn));
  J_K_Flip_Flop j_k_ff_3 (
    .J(1'b1), .clk(j_k_ff_2_q), .K(1'b1), .Q(j_k_ff_3_q), .Qn(j_k_ff_3_qn), .preset(or_1_out));  // open: en, reset
  J_K_Flip_Flop j_k_ff_4 (
    .J(1'b1), .clk(j_k_ff_3_q), .K(1'b1), .Qn(j_k_ff_4_qn), .preset(or_1_out));  // open: Q, en, reset
  and and_1 (and_1_out, j_k_ff_1_qn, not_1_out, j_k_ff_4_qn);
  or or_1 (or_1_out, and_1_out, and_2_out);
  and and_2 (and_2_out, in_1, j_k_ff_1_qn, j_k_ff_4_qn, j_k_ff_3_qn);
endmodule
