// Logisim project licznik synch rewers.circ as structural Verilog: 1 circuit, main circuit licznik synch. rewers.
module licznik_synch__rewers (
  input  switch
);

  wire _0_q, _1_q, _1_qn, _2_q, _2_qn, clock_out, nand_1_out, nand_2_out, nand_3_out, nand_4_out, nand_5_out,
       nand_6_out, not_1_out, reset_out;

  not not_1 (not_1_out, switch);
  Button clock (.out(clock_out));
  Button reset (.out(reset_out));
  J_K_Flip_Flop _2 (
    .J(nand_3_out), .clk(clock_out), .K(nand_3_out), .Q(_2_q), .Qn(_2_qn), .preset(reset_out));  // open: en, reset
  nand nand_1 (nand_1_out, switch, _1_q);
  nand nand_2 (nand_2_out, not_1_out, _1_qn);
  nand nand_3 (nand_3_out, nand_1_out, nand_2_out);
  LED x1 (.in(_1_q));
  LED x2 (.in(_2_q));
  LED x0 (.in(_0_q));
  J_K_Flip_Flop _1 (.J(1'b1), .clk(clock_out), .K(1'b1), .Q(_1_q), .Qn(_1_qn), .preset(reset_out));  // open: en, reset
  J_K_Flip_Flop _0 (
    .J(nand_6_out), .clk(clock_out), .K(nand_6_out), .Q(_0_q), .reset(reset_out));  // open: Qn, preset, en
  nand nand_4 (nand_4_out, switch, _1_q, _2_q);
  nand nand_5 (nand_5_out, not_1_out, _1_qn, _2_qn);
  nand nand_6 (nand_6_out, nand_4_out, nand_5_out);
endmodule
