// Logisim project reszta z dzielenia przez 4 bez zegara.circ as structural Verilog: 1 circuit, main circuit main
module main (
);

  wire _0_out, _1_out, JK0_q, JK0_qn, JK1_q, nor_1_out, nor_2_out, not_1_out, not_2_out, reset_out;

  Button _0 (.out(_0_out));
  Button _1 (.out(_1_out));
  Button reset (.out(reset_out));
  nor nor_1 (nor_1_out, _1_out, _0_out);
  not not_1 (not_1_out, nor_1_out);
  J_K_Flip_Flop JK1 (.J(JK0_q), .clk(not_1_out), .K(JK0_qn), .Q(JK1_q), .reset(reset_out));  // open: Qn, preset, en
  LED Y1 (.in(JK1_q));
  LED Y0 (.in(JK0_q));
  nor nor_2 (nor_2_out, _1_out, _0_out);
  not not_2 (not_2_out, nor_2_out);
  J_K_Flip_Flop JK0 (
    .J(_1_out), .clk(not_2_out), .K(_0_out), .Q(JK0_q), .Qn(JK0_qn), .reset(reset_out));  // open: preset, en
endmodule
