// Logisim project reszta z dzielenia przez 4.circ as structural Verilog: 1 circuit, main circuit main
module main (
  input  X
);

  wire clock_out, JK0_q, JK0_qn, JK1_q, not_1_out, not_2_out, reset_out;

  Button clock (.out(clock_out));
  Button reset (.out(reset_out));
  not not_1 (not_1_out, reset_out);
  J_K_Flip_Flop JK1 (.J(JK0_q), .clk(clock_out), .K(JK0_qn), .Q(JK1_q), .reset(not_1_out));  // open: Qn, preset, en
  not not_2 (not_2_out, X);
  LED Y0 (.in(JK0_q));
  LED Y1 (.in(JK1_q));
  J_K_Flip_Flop JK0 (
    .J(X), .clk(clock_out), .K(not_2_out), .Q(JK0_q), .Qn(JK0_qn), .reset(not_1_out));  // open: preset, en
endmodule
