// Logisim project 206-and_or.circ as structural Verilog: 1 circuit, main circuit main
module main (
  input  P,
  input  Z
);

  wire and_1_out, and_2_out, and_3_out, and_4_out, and_5_out, and_6_out, and_7_out, and_8_out, and_9_out,
       and_10_out, and_11_out, CLOCK_out, JK0_q, JK0_qn, JK1_q, JK1_qn, or_1_out, or_2_out, or_3_out,
       P_2_out, P_out, S0_out, S1_out;

  Button CLOCK (.out(CLOCK_out));
  and and_1 (and_1_out, P, Z);
  and and_2 (and_2_out, Z, JK1_q, JK0_q);
  and and_3 (and_3_out, P_out, Z, JK1_qn, JK0_qn);
  and and_4 (and_4_out, P_out, P_2_out, JK1_qn, JK0_q);
  and and_5 (and_5_out, P_2_out, P_out, JK1_q, JK0_qn);
  not u_P (P_out, P);
  not P_2 (P_2_out, Z);
  or or_1 (or_1_out, and_1_out, and_2_out, and_3_out, and_4_out, and_5_out);
  and and_6 (and_6_out, P_out, Z, JK1_q, JK0_qn);
  not S1 (S1_out, and_6_out);
  not S0 (S0_out, or_1_out);
  and and_7 (and_7_out, JK0_q, or_1_out);
  and and_8 (and_8_out, S1_out, S0_out);
  J_K_Flip_Flop JK1 (.J(and_7_out), .clk(CLOCK_out), .K(and_8_out), .Q(JK1_q), .Qn(JK1_qn));  // open: preset, en, reset
  and and_9 (and_9_out, and_6_out, JK1_q);
  and and_10 (and_10_out, or_1_out, JK1_qn);
  or or_2 (or_2_out, and_9_out, and_10_out);
  LED B0 (.in(JK0_q));
  LED B1 (.in(JK1_q));
  J_K_Flip_Flop #(.trigger("falling")) JK0 (
    .J(or_2_out), .clk(CLOCK_out), .K(1'b1), .Q(JK0_q), .Qn(JK0_qn));  // open: preset, en, reset
  LED Y (.in(or_3_out));
  or or_3 (or_3_out, JK0_q, and_11_out);
  and and_11 (and_11_out, P, JK1_q, JK0_qn);
endmodule
