// Logisim project 206-poprawiona.circ as structural Verilog: 1 circuit, main circuit main
module main (
  input  P,
  input  Z
);

  wire CLOCK_out, JK0_q, JK1_q, nand_1_out, nand_2_out, nand_3_out, nand_4_out, nand_5_out, nand_6_out,
       nand_7_out, nand_8_out, nand_9_out, nand_10_out, nand_11_out, nor_1_out, nor_2_out, nor_3_out,
       nor_4_out, not_1_out, not_2_out, not_3_out, not_4_out, not_5_out, not_6_out, not_7_out, not_8_out;

  LED B1 (.in(JK1_q));
  Button CLOCK (.out(CLOCK_out));
  LED B0 (.in(JK0_q));
  not not_1 (not_1_out, P);
  not not_2 (not_2_out, Z);
  not not_3 (not_3_out, JK0_q);
  not not_4 (not_4_out, JK1_q);
  nand nand_1 (nand_1_out, P, JK1_q, not_3_out);
  nand nand_2 (nand_2_out, nand_1_out, not_3_out);
  nand nand_3 (nand_3_out, Z, JK1_q, JK0_q);
  nand nand_4 (nand_4_out, not_1_out, Z, not_4_out, not_3_out);
  nand nand_5 (nand_5_out, not_1_out, not_2_out, not_4_out, JK0_q);
  nand nand_6 (nand_6_out, not_1_out, not_2_out, JK1_q, not_3_out);
  nor nor_1 (nor_1_out, not_1_out, not_2_out);
  nand nand_7 (nand_7_out, not_1_out, Z, JK1_q, not_3_out);
  LED Y (.in(nand_2_out));
  nand nand_8 (nand_8_out, nand_3_out, nand_4_out, nand_5_out, nand_6_out);
  not not_5 (not_5_out, nand_7_out);
  nor nor_2 (nor_2_out, nand_8_out, nor_1_out);
  not not_6 (not_6_out, nor_2_out);
  not not_7 (not_7_out, not_5_out);
  not not_8 (not_8_out, not_6_out);
  nor nor_3 (nor_3_out, not_3_out, not_8_out);
  nor nor_4 (nor_4_out, not_6_out, not_5_out);
  nand nand_9 (nand_9_out, not_6_out, not_4_out);
  nand nand_10 (nand_10_out, JK1_q, not_5_out);
  nand nand_11 (nand_11_out, nand_9_out, nand_10_out);
  J_K_Flip_Flop JK1 (.J(nor_3_out), .clk(CLOCK_out), .K(nor_4_out), .Q(JK1_q));  // open: Qn, preset, en, reset
  J_K_Flip_Flop #(.trigger("falling")) JK0 (
    .J(nand_11_out), .clk(CLOCK_out), .K(1'b1), .Q(JK0_q));  // open: Qn, preset, en, reset

  // Notes on the sheet:
  //   Z
  //   P
  //   Q1
  //   Q0
  //   S1
  //   S0
endmodule
