// Logisim project licznik asynch mod 9-13 v2.circ as structural Verilog: 1 circuit, main circuit licznik asynch mod 9/13
module licznik_asynch_mod_9_13 (
  input  switch_9_13
);

  wire clock_out, j_k_ff_1_q, j_k_ff_1_qn, j_k_ff_2_q, j_k_ff_2_qn, j_k_ff_3_q, j_k_ff_3_qn, j_k_ff_4_qn,
       NAND1_out, NAND2_out, NAND3_out, NAND4_out, NOR1_out, NOR2_out, NOT1_out, NOT2_out, NOT3_out,
       reset_out;

  Button clock (.out(clock_out));
  Button reset (.out(reset_out));
  J_K_Flip_Flop j_k_ff_1 (
    .J(1'b1), .clk(clock_out), .K(1'b1), .Q(j_k_ff_1_q), .Qn(j_k_ff_1_qn), .preset(NOT2_out));  // open: en, reset
  LED x2 (.in(j_k_ff_3_qn));
  LED x3 (.in(j_k_ff_4_qn));
  J_K_Flip_Flop j_k_ff_2 (
    .J(1'b1), .clk(j_k_ff_1_q), .K(1'b1), .Q(j_k_ff_2_q), .Qn(j_k_ff_2_qn), .preset(NOT2_out));  // open: en, reset
  LED x0 (.in(j_k_ff_1_qn));
  LED x1 (.in(j_k_ff_2_qn));
  J_K_Flip_Flop j_k_ff_3 (
    .J(1'b1), .clk(j_k_ff_2_q), .K(1'b1), .Q(j_k_ff_3_q), .Qn(j_k_ff_3_qn), .preset(NOT2_out));  // open: en, reset
  not NOT1 (NOT1_out, switch_9_13);
  nand NAND3 (NAND3_out, switch_9_13, j_k_ff_1_qn);
  nand NAND4 (NAND4_out, j_k_ff_4_qn, j_k_ff_3_qn);
  J_K_Flip_Flop j_k_ff_4 (
    .J(1'b1), .clk(j_k_ff_3_q), .K(1'b1), .Qn(j_k_ff_4_qn), .preset(NOT2_out));  // open: Q, en, reset
  nand NAND1 (NAND1_out, NOT1_out, j_k_ff_1_qn, j_k_ff_4_qn);
  nor NOR2 (NOR2_out, NAND3_out, NAND4_out);
  not NOT3 (NOT3_out, reset_out);
  nand NAND2 (NAND2_out, NAND1_out, NOT3_out);
  nor NOR1 (NOR1_out, NAND2_out, NOR2_out);
  not NOT2 (NOT2_out, NOR1_out);
endmodule
