// Logisim project licznik asynch mod 9-13 v3 (poprawa).circ as structural Verilog: 1 circuit, main circuit licznik asynch mod 9/13
module licznik_asynch_mod_9_13 (
  input  switch_9_13
);

  wire clock_out, j_k_ff_1_q, j_k_ff_1_qn, j_k_ff_2_q, j_k_ff_2_qn, j_k_ff_3_q, j_k_ff_3_qn, j_k_ff_4_q,
       NAND1_out, NAND2_out, NAND3_out, NAND4_out, NAND5_out, NOR1_out, NOR2_out, reset_out;

  Button clock (.out(clock_out));
  Button reset (.out(reset_out));
  J_K_Flip_Flop #(.trigger("falling")) j_k_ff_1 (
    .J(1'b1), .clk(clock_out), .K(1'b1), .Q(j_k_ff_1_q), .Qn(j_k_ff_1_qn), .reset(NOR2_out));  // open: preset, en
  LED x3 (.in(j_k_ff_4_q));
  LED x2 (.in(j_k_ff_3_q));
  J_K_Flip_Flop #(.trigger("falling")) j_k_ff_2 (
    .J(1'b1), .clk(j_k_ff_1_q), .K(1'b1), .Q(j_k_ff_2_q), .Qn(j_k_ff_2_qn), .reset(NOR2_out));  // open: preset, en
  LED x0 (.in(j_k_ff_1_q));
  LED x1 (.in(j_k_ff_2_q));
  J_K_Flip_Flop #(.trigger("falling")) j_k_ff_3 (
    .J(1'b1), .clk(j_k_ff_2_q), .K(1'b1), .Q(j_k_ff_3_q), .Qn(j_k_ff_3_qn), .reset(NOR2_out));  // open: preset, en
  J_K_Flip_Flop #(.trigger("falling")) j_k_ff_4 (
    .J(1'b1), .clk(j_k_ff_3_q), .K(1'b1), .Q(j_k_ff_4_q), .reset(NOR2_out));  // open: Qn, preset, en
  nand NAND1 (NAND1_out, j_k_ff_1_qn, j_k_ff_2_qn, j_k_ff_3_qn);
  nand NAND3 (NAND3_out, switch_9_13, j_k_ff_2_qn, j_k_ff_1_qn);
  nand NAND4 (NAND4_out, switch_9_13, j_k_ff_3_qn);
  nand NAND2 (NAND2_out, NAND1_out, j_k_ff_4_q);
  nand NAND5 (NAND5_out, NAND3_out, NAND4_out);
  nor NOR1 (NOR1_out, NAND2_out, NAND5_out);
  nor NOR2 (NOR2_out, NOR1_out, reset_out);
endmodule
