// Logisim project schemat-205-dzialajacy.circ as structural Verilog: 1 circuit, main circuit main
module main (
  input  in_1,
  input  in_2
);

  wire button_1_out, button_2_out, j_k_ff_1_q, j_k_ff_1_qn, j_k_ff_2_q, j_k_ff_2_qn, j_k_ff_3_q, j_k_ff_3_qn,
       nand_1_out, nand_2_out, nand_3_out, nand_4_out, nand_5_out, nand_6_out, nand_7_out, nand_8_out,
       nand_9_out, nand_10_out, nand_11_out, nor_1_out, nor_2_out, not_1_out, not_2_out, not_3_out,
       not_4_out, not_5_out, not_6_out, not_7_out;

  Button button_1 (.out(button_1_out));
  not not_1 (not_1_out, in_2);
  Button button_2 (.out(button_2_out));
  not not_2 (not_2_out, nand_1_out);
  nand nand_1 (nand_1_out, not_3_out, nand_3_out);
  J_K_Flip_Flop j_k_ff_1 (
    .J(not_2_out), .clk(button_1_out), .K(nand_2_out), .Q(j_k_ff_1_q), .Qn(j_k_ff_1_qn), .reset(button_2_out));  // open: preset, en
  nand nand_2 (nand_2_out, j_k_ff_3_q, j_k_ff_1_q, j_k_ff_2_qn);
  not not_3 (not_3_out, nor_1_out);
  nand nand_3 (nand_3_out, j_k_ff_1_qn, j_k_ff_3_qn, not_1_out);
  nor nor_1 (nor_1_out, j_k_ff_1_q, j_k_ff_2_q);
  J_K_Flip_Flop j_k_ff_2 (
    .J(nand_5_out), .clk(button_1_out), .K(in_1), .Q(j_k_ff_2_q), .Qn(j_k_ff_2_qn), .reset(button_2_out));  // open: preset, en
  nand nand_4 (nand_4_out, j_k_ff_1_qn, j_k_ff_3_q, in_2);
  nand nand_5 (nand_5_out, j_k_ff_2_qn, nand_4_out, not_4_out);
  not not_4 (not_4_out, nor_2_out);
  nor nor_2 (nor_2_out, j_k_ff_3_q, in_2);
  nand nand_6 (nand_6_out, not_1_out, j_k_ff_3_qn, j_k_ff_2_q, j_k_ff_1_qn);
  not not_5 (not_5_out, nand_7_out);
  nand nand_7 (nand_7_out, nand_8_out, nand_9_out);
  J_K_Flip_Flop j_k_ff_3 (
    .J(nand_6_out), .clk(button_1_out), .K(not_5_out), .Q(j_k_ff_3_q), .Qn(j_k_ff_3_qn), .reset(button_2_out));  // open: preset, en
  nand nand_8 (nand_8_out, j_k_ff_1_q, j_k_ff_2_qn, j_k_ff_3_q);
  nand nand_9 (nand_9_out, j_k_ff_1_qn, j_k_ff_2_q, j_k_ff_3_q, not_1_out);
  LED y1 (.in(not_6_out));
  not not_6 (not_6_out, nand_10_out);
  nand nand_10 (nand_10_out, j_k_ff_1_q, j_k_ff_2_qn, j_k_ff_3_qn);
  LED y0 (.in(not_7_out));
  not not_7 (not_7_out, nand_11_out);
  nand nand_11 (nand_11_out, j_k_ff_1_q, j_k_ff_2_qn, j_k_ff_3_q);
endmodule
